# Fritzing sketch Binary clock with stop watch (1) (saved by Fritzing 0.9.3b)
breadboards: 2

parts:
  Part1 = Arduino Uno (Rev3) - ICSP
  LED2 = smd LED [color="Red (633nm)" package="1206 [SMD]"]
  LED6 = smd LED [color="Orange (605nm)" package="1206 [SMD]"]
  LED7 = smd LED [color="Green (560nm)" package="1206 [SMD]"]
  S1 = Pushbutton [package="[SMD]"]
  S2 = Pushbutton [package="[SMD]"]
  R1 = Resistor [tolerance=±5% resistance=10k package=THT]
  LED18 = smd LED [color="Red (633nm)" package="1206 [SMD]"]
  LED19 = smd LED [color="Red (633nm)" package="1206 [SMD]"]
  LED20 = smd LED [color="Red (633nm)" package="1206 [SMD]"]
  LED21 = smd LED [color="Red (633nm)" package="1206 [SMD]"]
  R2 = Resistor [tolerance=±5% resistance=100 package=THT]
  R3 = Resistor [tolerance=±5% resistance=100 package=THT]
  R4 = Resistor [tolerance=±5% resistance=100 package=THT]
  R5 = Resistor [tolerance=±5% resistance=100 package=THT]
  R6 = Resistor [tolerance=±5% resistance=100 package=THT]
  R7 = Resistor [tolerance=±5% resistance=100 package=THT]
  R8 = Resistor [tolerance=±5% resistance=10k package=THT]
  LED22 = smd LED [color="Orange (605nm)" package="1206 [SMD]"]
  LED23 = smd LED [color="Orange (605nm)" package="1206 [SMD]"]
  LED24 = smd LED [color="Orange (605nm)" package="1206 [SMD]"]
  LED25 = smd LED [color="Orange (605nm)" package="1206 [SMD]"]
  LED26 = smd LED [color="Orange (605nm)" package="1206 [SMD]"]
  LED27 = smd LED [color="Green (560nm)" package="1206 [SMD]"]
  LED28 = smd LED [color="Green (560nm)" package="1206 [SMD]"]
  LED29 = smd LED [color="Green (560nm)" package="1206 [SMD]"]
  LED30 = smd LED [color="Green (560nm)" package="1206 [SMD]"]
  LED31 = smd LED [color="Green (560nm)" package="1206 [SMD]"]
  R9 = Resistor [tolerance=±5% resistance=100 package=THT]
  R10 = Resistor [tolerance=±5% resistance=100 package=THT]
  R11 = Resistor [tolerance=±5% resistance=100 package=THT]
  R12 = Resistor [tolerance=±5% resistance=100 package=THT]
  R13 = Resistor [tolerance=±5% resistance=100 package=THT]
  R14 = Resistor [tolerance=±5% resistance=100 package=THT]
  R15 = Resistor [tolerance=±5% resistance=100 package=THT]
  R16 = Resistor [tolerance=±5% resistance=100 package=THT]
  R17 = Resistor [tolerance=±5% resistance=100 package=THT]
  R18 = Resistor [tolerance=±5% resistance=100 package=THT]
  R19 = Resistor [tolerance=±5% resistance=100 package=THT]

nets:
  N1: Part1.A0, S1.Pin_1, S1.Pin_2, R1.Pin_0
  N2: Part1.D8, LED27.anode
  N3: Part1.D9_PWM, LED29.anode
  N4: Part1.D10_PWM/SS, LED28.anode
  N5: Part1.D11_PWM/MOSI, LED31.anode
  N6: Part1.D12/MISO, LED30.anode
  N7: Part1.D13/SCK, S2.Pin_1, S2.Pin_2, R8.Pin_0
  N8: Part1.D0/RX, LED6.anode
  N9: Part1.D2, LED22.anode
  N10: Part1.D3_PWM, LED23.anode
  N11: Part1.D4, LED24.anode
  N12: Part1.D5_PWM, LED25.anode
  N13: Part1.D6_PWM, LED26.anode
  N14: Part1.D7, LED7.anode
  N15: Part1.5V, S1.Pin_3, S1.Pin_4, S2.Pin_3, S2.Pin_4
  N16: Part1.GND, R1.Pin_1, R2.Pin_1, R3.Pin_1, R4.Pin_1, R5.Pin_1, R6.Pin_1, R7.Pin_1, R8.Pin_1, R9.Pin_1, R10.Pin_1, R11.Pin_1, R12.Pin_1, R13.Pin_1, R14.Pin_1, R15.Pin_1, R16.Pin_1, R17.Pin_1, R18.Pin_1, R19.Pin_1
  N17: LED2.cathode, R7.Pin_0
  N18: LED6.cathode, R6.Pin_0
  N19: LED7.cathode, R14.Pin_0
  N20: LED18.cathode, R2.Pin_0
  N21: LED19.cathode, R4.Pin_0
  N22: LED20.cathode, R3.Pin_0
  N23: LED21.cathode, R5.Pin_0
  N24: LED22.cathode, R9.Pin_0
  N25: LED23.cathode, R10.Pin_0
  N26: LED24.cathode, R11.Pin_0
  N27: LED25.cathode, R12.Pin_0
  N28: LED26.cathode, R13.Pin_0
  N29: LED27.cathode, R15.Pin_0
  N30: LED28.cathode, R17.Pin_0
  N31: LED29.cathode, R16.Pin_0
  N32: LED30.cathode, R18.Pin_0
  N33: LED31.cathode, R19.Pin_0

// code stored in the sketch: Binary_clock with stopwatch2.ino
/*  Binary Clock & Stopwatch Project                   */
/*  The project is implemented using Arduino uno       */
/*  authors:                                           */
/*  Full project:                                      */


/* Variable declartion and Pin configrations*/
struct Time {  
  uint8_t Hour;
  uint8_t Minute;
  uint8_t Second;
};


Time Clock     = { 0, 0, 0 };  // initialize clock instance
Time StopWatch = { 0, 0, 0 };  // initialize stopwatch instance


int LedSeconds[] = {7,8,9,10,11,12}; 
int LedMinutes[] = {0,1,2,3,4,5};    
int LedHours[]   = {A1,A2,A3,A4,A5};   


const int ModeSelect = A0;  // the button to select mode between clock & stopwatch 
const int FunSelect  = 6;   // the button to select between functionalities in stopwatch 
int But_State1 = 0;  // state of button to detect changes
int But_State2 = 0;  // state of button to detect changes


int start_en = 0;  // the moment the button was pressed
uint8_t end_en = 0;    // the moment the button was released
uint8_t period_en = 0;   // how long the button was idle


bool Mode  = true;     // run selected mode clock or stopwatch
bool TimeRun   = true; // display time in binary on leds


int nBitsSeconds;
int nBitsMinutes;
int nBitsHours;


/*Mode selection between clock and stopwatch */
void ModeSelectionISR()
 {
  But_State1++;
  if (But_State1 % 2 != 0) 
  {
    StopWatch = { 0, 0, 0 };  //StopWatch Mode
    Mode = false;
  } else {
    Mode = true;              //Normal Mode 
    }
}


/* Selects the mode of execution of stop-watch i.e pause, resume, reset
   1) pause = odd # of buttons presses
   2) resume = even # of button presses
   3) reset = pressed twice within time limit */
void FunSelectionISR() {
  if (But_State1 % 2 != 0) {
     But_State2++;
    if (But_State2 % 2 != 0) {          //pause
        start_en = millis();
        TimeRun = false;
        Mode = true;
    } else {                
      end_en = millis();              //resume
      period_en = end_en - start_en;
      start_en, end_en =0;
      if (period_en < 1000) {
        StopWatch = { 0, 0, 0 };          //reset
      }
        TimeRun = true;
        Mode = false;
    }
  }
}


// Pin cofigration
void setup(void)
{


   nBitsSeconds = sizeof(LedSeconds)/sizeof(LedSeconds[0]) ;
   nBitsMinutes = sizeof(LedMinutes)/sizeof(LedMinutes[0]);
   nBitsHours = sizeof(LedHours)/sizeof(LedHours[0]);


  for (byte i = 0; i < nBitsSeconds; i++) {
    pinMode(LedSeconds[i], OUTPUT);
  }


  for (byte i = 0; i < nBitsMinutes; i++) {
    pinMode(LedMinutes[i], OUTPUT);
  }


  for (byte i = 0; i < nBitsHours; i++) {
    pinMode(LedHours[i], OUTPUT);
  }
  
  pinMode(ModeSelect, INPUT_PULLUP);
  attachInterrupt(digitalPinToInterrupt(ModeSelect), ModeSelectionISR, RISING);
  
  pinMode(FunSelect, INPUT_PULLUP);
  attachInterrupt(digitalPinToInterrupt(FunSelect), FunSelectionISR, RISING);
}


/*  the main routine*/
void loop(void)
{
  if (Mode){                                                  //clock mode
    Tick(Clock);                                           
    Clock.Hour = (Clock.Hour + StopWatch.Hour) % 24;               
    Clock.Minute = (Clock.Minute + StopWatch.Minute) % 60;          
    Clock.Second = (Clock.Second + StopWatch.Second) % 60;             
    if (TimeRun) {                                         
      displayBinarySeconds(Clock.Second);
      displayBinaryMinutes(Clock.Minute);
      displayBinaryHours(Clock.Hour);
    }
  } else {
    Tick(StopWatch);                                       //sw-mode
     if (TimeRun) {                                         //display time
      displayBinarySeconds(StopWatch.Second);
      displayBinaryMinutes(StopWatch.Minute);
      displayBinaryHours(StopWatch.Hour);
    }
  }
  delay(1000);   // 1000 milliseconds = approx. 1 second delay
}


// displays time seconds, minutes and hours
void displayBinarySeconds(byte nSec)
{
  for (byte i = 0; i < nBitsSeconds; i++) {
    digitalWrite(LedSeconds[i], nSec & 1);
    nSec /= 2;
  }
}


void displayBinaryMinutes(byte nMin)
{
  for (byte i = 0; i < nBitsMinutes; i++) {
    digitalWrite(LedMinutes[i], nMin & 1);
    nMin /= 2;
  }
}


void displayBinaryHours(byte nHr)
{
  for (byte i = 0; i < nBitsHours; i++) {
    digitalWrite(LedHours[i], nHr & 1);
    nHr /= 2;
  }
}


// Calculates time, increments secends,minutes and hours counters
void Tick(struct Time &Temp){
  Temp.Second = (Temp.Second + 1);
  if (Temp.Second > 59)
  {
    Temp.Second = 0;
    Temp.Minute = (Temp.Minute + 1);
    if (Temp.Minute > 59)
    {
      Temp.Minute = 0;
      Temp.Hour = (Temp.Hour + 1);
      if (Temp.Hour > 23)
      {
        Temp.Hour = 0;
        Temp.Minute = 0;
        Temp.Second = 0;
      }
    }
  }
}
